# Fritzing sketch timer (saved by Fritzing 0.9.10b)
breadboards: 1

parts:
  Mod1 = Raspberry Pi 4B
  R1 = Resistor [tolerance=±5% resistance=220 package="2512 [SMD]"]
  R5 = Resistor [tolerance=±5% resistance=220 package="2512 [SMD]"]
  LED1 = LED - 3mm [color="Red (633nm)" current=30mA package="3 mm [THT]"]
  LED2 = LED - 3mm [color="Red (633nm)" current=30mA package="3 mm [THT]"]
  LED3 = LED - 3mm [color="Red (633nm)" current=30mA package="3 mm [THT]"]
  R6 = Resistor [tolerance=±5% resistance=220 package="2512 [SMD]"]
  R7 = Resistor [tolerance=±5% resistance=220 package="2512 [SMD]"]
  S1 = Pushbutton [package="[THT]"]
  S2 = SWITCH_SPDT [package=kps-1290]
  LED5 = LED - 5mm [color="White (4500K)" current=0.030 package="5 mm [THT]"]
  R8 = Resistor [tolerance=±5% resistance=220 package="2512 [SMD]"]

nets:
  N1: Mod1.3V3, R7.Pin_1, S2.P
  N2: Mod1.GPIO2, R1.Pin_1
  N3: Mod1.GPIO3, R5.Pin_1
  N4: Mod1.GND, LED1.cathode, LED2.cathode, LED3.cathode, LED5.cathode
  N5: Mod1.GPIO4, R6.Pin_1
  N6: Mod1.GPIO17, S1.Pin_3, S1.Pin_4
  N7: Mod1.GPIO27, S2.S, R8.Pin_1
  N8: R1.Pin_0, LED1.anode
  N9: R5.Pin_0, LED2.anode
  N10: LED3.anode, R6.Pin_0
  N11: R7.Pin_0, S1.Pin_1, S1.Pin_2
  N12: LED5.anode, R8.Pin_0

notes:
  GPIO pins used:
  Pin 1 -> 3.3v rail
  Pin 3 -> J2
  Pin 5 -> I3
  Pin 6 -> Ground rail
  Pin 7 -> H4
  Pin 11 -> J6
  Pin 13 -> J24
